// Logisim project NOR.circ as structural Verilog: 1 circuit, main circuit main
module main (
  input  in_1,
  input  in_2,
  input  in_3,
  input  in_4,
  output out_5,
  output out_6
);

  wire nor_1_out, nor_2_out, nor_3_out, nor_4_out, nor_5_out, nor_6_out, nor_7_out;

  nor nor_1 (nor_1_out, in_1, in_2);
  nor nor_2 (nor_2_out, in_3, in_4);
  nor nor_3 (nor_3_out, in_1, nor_1_out);
  nor nor_4 (nor_4_out, nor_1_out, in_2);
  nor nor_5 (nor_5_out, in_3, nor_2_out);
  nor nor_6 (nor_6_out, nor_2_out, in_4);
  nor nor_7 (nor_7_out, nor_3_out, nor_4_out);
  nor nor_8 (out_6, nor_5_out, nor_6_out);
  nor nor_9 (out_5, nor_7_out, nor_7_out);

  // Notes on the sheet:
  //   X-OR
  //   X-NOR
endmodule
