// Logisim project universal-gate.circ as structural Verilog: 1 circuit, main circuit main
module main (
  input  in_1,
  input  in_2,
  input  in_3,
  input  in_4,
  input  in_5,
  input  in_6,
  input  in_7,
  input  in_8,
  input  in_9,
  input  in_10,
  output out_11,
  output out_12,
  output out_13,
  output out_14,
  output out_15,
  output out_16
);

  wire nand_1_out, nand_2_out, nand_3_out, nor_1_out, nor_2_out, nor_4_out;

  nand nand_1 (nand_1_out, in_3, in_5);
  nand nand_2 (nand_2_out, in_7, in_7);
  nand nand_3 (nand_3_out, in_9, in_9);
  nand nand_4 (out_12, in_2, in_2);
  nand nand_5 (out_13, nand_1_out, nand_1_out);
  nand nand_6 (out_15, nand_2_out, nand_3_out);
  nor nor_1 (nor_1_out, in_8, in_8);
  nor nor_2 (nor_2_out, in_10, in_10);
  nor nor_3 (out_11, in_1, in_1);
  nor nor_4 (nor_4_out, in_4, in_6);
  nor nor_5 (out_14, nor_4_out, nor_4_out);
  nor nor_6 (out_16, nor_1_out, nor_2_out);

  // Notes on the sheet:
  //   OR-GATE
  //   NOT-GATE
  //   AND-GATE
  //   AND-GATE
  //   NOT-GATE
  //   OR-GATE
endmodule
