// Logisim project 4 bit adder.circ as structural Verilog: 3 circuits, main circuit main
module main (
  input  A4,
  input  A3,
  input  A2,
  input  A1,
  input  B4,
  input  B3,
  input  B2,
  input  B1,
  input  M,
  output Output_carry,
  output [3:0] out_11
);

  wire ic_7486_1_out_9, ic_7486_1_out_10, ic_7486_1_out_11, ic_7486_1_out_12;

  IC_74283 ic_74283_1 (
    .in_1(M), .A1(A1), .B1(ic_7486_1_out_12), .A2(A2), .B2(ic_7486_1_out_11), .A3(A3), .B3(ic_7486_1_out_10),
    .A4(A4), .B4(ic_7486_1_out_9), .out_10(out_11), .out_11(Output_carry));
  IC_7486 ic_7486_1 (
    .in_1(B4), .in_2(M), .in_3(B3), .in_4(M), .in_5(B2), .in_6(M), .in_7(B1), .in_8(M),
    .out_9(ic_7486_1_out_9), .out_10(ic_7486_1_out_10), .out_11(ic_7486_1_out_11), .out_12(ic_7486_1_out_12));

  // Notes on the sheet:
  //   M=0 for Add
  //                         M=1 for substract
  //   output
endmodule

module IC_74283 (
  input  in_1,
  input  A1,
  input  B1,
  input  A2,
  input  B2,
  input  A3,
  input  B3,
  input  A4,
  input  B4,
  output [3:0] out_10,
  output out_11
);

  wire adder_1_cout, adder_2_cout, adder_3_cout;

  Adder #(.width(1)) adder_1 (.a(A1), .b(B1), .out(out_10[0]), .cin(in_1), .cout(adder_1_cout));
  Adder #(.width(1)) adder_2 (.a(A2), .b(B2), .out(out_10[1]), .cin(adder_1_cout), .cout(adder_2_cout));
  Adder #(.width(1)) adder_3 (.a(A3), .b(B3), .out(out_10[2]), .cin(adder_2_cout), .cout(adder_3_cout));
  Adder #(.width(1)) adder_4 (.a(A4), .b(B4), .out(out_10[3]), .cin(adder_3_cout), .cout(out_11));
endmodule

module IC_7486 (
  input  in_1,
  input  in_2,
  input  in_3,
  input  in_4,
  input  in_5,
  input  in_6,
  input  in_7,
  input  in_8,
  output out_9,
  output out_10,
  output out_11,
  output out_12
);

  xor xor_1 (out_9, in_1, in_2);
  xor xor_2 (out_10, in_3, in_4);
  xor xor_3 (out_11, in_5, in_6);
  xor xor_4 (out_12, in_7, in_8);
endmodule
