// Logisim project BCD adder circuit.circ as structural Verilog: 4 circuits, main circuit main
module main (
  input  in_1,
  input  in_2,
  input  in_3,
  input  in_4,
  input  in_5,
  input  in_6,
  input  in_7,
  input  in_8,
  input  in_9,
  input  in_10,
  output out_11,
  output out_12,
  output out_13,
  output out_14,
  output out_15
);

  wire ic_7408_1_out_9, ic_7408_1_out_12, ic_7432_1_out_12, ic_74283_1_out_14, ic_74283_1_s1, ic_74283_1_s2,
       ic_74283_1_s3, ic_74283_1_s4;

  IC_74283 ic_74283_1 (
    .in_1(in_10), .A1(in_5), .B1(in_9), .A2(in_4), .B2(in_8), .A3(in_3), .B3(in_7), .A4(in_2), .B4(in_6),
    .out_14(ic_74283_1_out_14), .S1(ic_74283_1_s1), .S2(ic_74283_1_s2), .S3(ic_74283_1_s3), .S4(ic_74283_1_s4));
  IC_74283 ic_74283_2 (
    .A1(in_1), .B1(ic_74283_1_s1), .A2(out_11), .B2(ic_74283_1_s2), .A3(out_11), .B3(ic_74283_1_s3),
    .A4(in_1), .B4(ic_74283_1_s4), .S1(out_15), .S2(out_14), .S3(out_13), .S4(out_12));  // open: in_1, out_14
  IC_7432 ic_7432_1 (
    .in_5(ic_7432_1_out_12), .in_6(ic_74283_1_out_14), .in_7(ic_7408_1_out_9), .in_8(ic_7408_1_out_12),
    .out_11(out_11), .out_12(ic_7432_1_out_12));  // open: in_1, in_2, in_3, in_4, out_9, out_10
  IC_7408 ic_7408_1 (
    .in_1(ic_74283_1_s2), .in_2(ic_74283_1_s4), .in_7(ic_74283_1_s3), .in_8(ic_74283_1_s4),
    .out_9(ic_7408_1_out_9), .out_12(ic_7408_1_out_12));  // open: in_3, in_4, in_5, in_6, out_10, out_11
endmodule

module IC_74283 (
  input  in_1,
  input  A1,
  input  B1,
  input  A2,
  input  B2,
  input  A3,
  input  B3,
  input  A4,
  input  B4,
  output S1,
  output S2,
  output S3,
  output S4,
  output out_14
);

  wire adder_1_cout, adder_2_cout, adder_3_cout;

  Adder #(.width(1)) adder_1 (.a(A1), .b(B1), .out(S1), .cin(in_1), .cout(adder_1_cout));
  Adder #(.width(1)) adder_2 (.a(A2), .b(B2), .out(S2), .cin(adder_1_cout), .cout(adder_2_cout));
  Adder #(.width(1)) adder_3 (.a(A3), .b(B3), .out(S3), .cin(adder_2_cout), .cout(adder_3_cout));
  Adder #(.width(1)) adder_4 (.a(A4), .b(B4), .out(S4), .cin(adder_3_cout), .cout(out_14));
endmodule

module IC_7408 (
  input  in_1,
  input  in_2,
  input  in_3,
  input  in_4,
  input  in_5,
  input  in_6,
  input  in_7,
  input  in_8,
  output out_9,
  output out_10,
  output out_11,
  output out_12
);

  and and_1 (out_9, in_1, in_2);
  and and_2 (out_10, in_3, in_4);
  and and_3 (out_11, in_5, in_6);
  and and_4 (out_12, in_7, in_8);
endmodule

module IC_7432 (
  input  in_1,
  input  in_2,
  input  in_3,
  input  in_4,
  input  in_5,
  input  in_6,
  input  in_7,
  input  in_8,
  output out_9,
  output out_10,
  output out_11,
  output out_12
);

  or or_1 (out_9, in_1, in_2);
  or or_2 (out_10, in_3, in_4);
  or or_3 (out_11, in_5, in_6);
  or or_4 (out_12, in_7, in_8);
endmodule
