// Logisim project boolean function .circ as structural Verilog: 2 circuits, main circuit main
module main (
  input  D,
  input  S0,
  input  S1,
  input  S3,
  output out_5
);

  IC_74151 ic_74151_1 (
    .I1(D), .I2(D), .I3(1'b0), .I4(1'b1), .I5(1'b0), .I6(1'b0), .I7(1'b1), .S0(S0), .S1(S1), .S3(S3),
    .Y(out_5), .I0(1'b1));
endmodule

module IC_74151 (
  input  I0,
  input  I1,
  input  I2,
  input  I3,
  input  I4,
  input  I5,
  input  I6,
  input  I7,
  input  S0,
  input  S1,
  input  S3,
  output Y
);

  Multiplexer #(.select(3)) multiplexer_1 (
    .in0(I0), .in1(I1), .in2(I2), .in3(I3), .in4(I4), .in5(I5), .in6(I6), .in7(I7), .out(Y),
    .sel({S3, S1, S0}));  // open: en
endmodule
