// Logisim project boolean function.circ as structural Verilog: 2 circuits, main circuit main
module main (
  input  in_1,
  input  _1,
  input  D,
  input  in_4,
  input  D_2,
  input  in_6,
  input  _1_2,
  input  _1_3,
  input  S0,
  input  S1,
  input  S3,
  output out_12
);

  IC_74151 ic_74151_1 (
    .in_2(D_2), .in_3(D), .in_4(in_1), .in_5(_1), .in_6(in_4), .in_7(in_6), .in_8(_1_3), .in_9(S0),
    .in_10(S1), .in_11(S3), .out_12(out_12), .in_1(_1_2));
endmodule

module IC_74151 (
  input  in_1,
  input  in_2,
  input  in_3,
  input  in_4,
  input  in_5,
  input  in_6,
  input  in_7,
  input  in_8,
  input  in_9,
  input  in_10,
  input  in_11,
  output out_12
);

  Multiplexer #(.select(3)) multiplexer_1 (
    .in0(in_1), .in1(in_2), .in2(in_3), .in3(in_4), .in4(in_5), .in5(in_6), .in6(in_7), .in7(in_8),
    .out(out_12), .sel({in_11, in_10, in_9}));  // open: en
endmodule
