// Logisim project decoder with boolean function.circ as structural Verilog: 1 circuit, main circuit main
module main (
  input  C,
  input  B,
  input  A,
  input  C_2,
  input  B_2,
  input  A_2,
  output Y0,
  output Y0_2,
  output Y1,
  output Y1_2,
  output Y2,
  output Y2_2,
  output Y3,
  output Y3_2,
  output Y4,
  output Y4_2,
  output Y5,
  output Y5_2,
  output Y6,
  output Y6_2,
  output Y7,
  output Y7_2
);

  wire not_1_out, not_2_out, not_3_out, not_4_out, not_5_out, not_6_out;

  not not_1 (not_1_out, B);
  not not_2 (not_2_out, C);
  not not_3 (not_3_out, A);
  nand nand_1 (Y0, not_2_out, not_1_out, not_3_out);
  nand nand_2 (Y1, not_2_out, not_1_out, A);
  nand nand_3 (Y2, not_2_out, B, not_3_out);
  nand nand_4 (Y3, not_2_out, B, A);
  nand nand_5 (Y4, C, not_1_out, not_3_out);
  nand nand_6 (Y5, C, not_1_out, A);
  nand nand_7 (Y6, C, B, not_3_out);
  nand nand_8 (Y7, C, B, A);
  not not_4 (not_4_out, B_2);
  not not_5 (not_5_out, C_2);
  not not_6 (not_6_out, A_2);
  and and_1 (Y0_2, not_5_out, not_4_out, not_6_out);
  and and_2 (Y1_2, not_5_out, not_4_out, A_2);
  and and_3 (Y2_2, not_5_out, B_2, not_6_out);
  and and_4 (Y3_2, not_5_out, B_2, A_2);
  and and_5 (Y4_2, C_2, not_4_out, not_6_out);
  and and_6 (Y5_2, C_2, not_4_out, A_2);
  and and_7 (Y6_2, C_2, B_2, not_6_out);
  and and_8 (Y7_2, C_2, B_2, A_2);

  // Notes on the sheet:
  //   Active low decoder
  //   Active high decoder
endmodule
