// Logisim project JK-Type.circ as structural Verilog: 1 circuit, main circuit main
module main (
  input  in_1,
  output out_2,
  output out_3,
  output out_4
);

  wire and_1_out, clock_1_out, j_k_ff_1_qn, j_k_ff_2_qn, not_1_out;

  not not_1 (not_1_out, in_1);
  Clock clock_1 (.out(clock_1_out));
  and and_1 (and_1_out, j_k_ff_1_qn, not_1_out);
  and and_2 (out_4, j_k_ff_1_qn, in_1);
  J_K_Flip_Flop j_k_ff_1 (
    .J(in_1), .clk(clock_1_out), .K(in_1), .Q(out_2), .Qn(j_k_ff_1_qn));  // open: preset, en, reset
  J_K_Flip_Flop j_k_ff_2 (
    .J(and_1_out), .clk(clock_1_out), .K(in_1), .Q(out_3), .Qn(j_k_ff_2_qn));  // open: preset, en, reset
endmodule
