// Logisim project T-Type.circ as structural Verilog: 1 circuit, main circuit main
module main (
  input  in_1,
  output out_2
);

  wire and_1_out, and_2_out, clock_1_out, not_1_out, or_1_out, t_ff_1_qn, t_ff_2_q, t_ff_2_qn;

  Clock clock_1 (.out(clock_1_out));
  not not_1 (not_1_out, in_1);
  and and_1 (and_1_out, t_ff_1_qn, t_ff_2_qn, not_1_out);
  or or_1 (or_1_out, and_1_out, and_2_out);
  T_Flip_Flop t_ff_1 (.clk(clock_1_out), .T(in_1), .Qn(t_ff_1_qn));  // open: Q, preset, reset, en
  T_Flip_Flop t_ff_2 (.clk(clock_1_out), .T(or_1_out), .Q(t_ff_2_q), .Qn(t_ff_2_qn));  // open: preset, reset, en
  and and_2 (and_2_out, in_1, t_ff_2_q);
  and and_3 (out_2, t_ff_1_qn, in_1);
endmodule
