// Logisim project Product-of-Maxterm.circ as structural Verilog: 4 circuits, main circuit main
module main (
  input  A,
  input  C,
  input  B,
  output out_4
);

  wire n3_input_and_1_out_12, n3_input_or_1_out_10, n3_input_or_1_out_11, n3_input_or_1_out_12,
       n3_input_or_2_out_11, n3_input_or_2_out_12, not_1_out_10, not_1_out_11, not_1_out_12;

  NOT not_1 (
    .in_4(B), .in_5(C), .in_6(A), .out_10(not_1_out_10), .out_11(not_1_out_11), .out_12(not_1_out_12));  // open: in_1, in_2, in_3, out_7, out_8, out_9
  _3_input_OR u_3_input_or_1 (
    .in_1(B), .in_2(C), .in_3(not_1_out_12), .in_4(not_1_out_10), .in_5(C), .in_6(not_1_out_12), .in_7(B),
    .in_8(C), .in_9(A), .out_10(n3_input_or_1_out_10), .out_11(n3_input_or_1_out_11),
    .out_12(n3_input_or_1_out_12));
  _3_input_AND u_3_input_and_1 (
    .in_4(n3_input_and_1_out_12), .in_5(n3_input_or_2_out_12), .in_6(n3_input_or_2_out_11),
    .in_7(n3_input_or_1_out_10), .in_8(n3_input_or_1_out_11), .in_9(n3_input_or_1_out_12), .out_11(out_4),
    .out_12(n3_input_and_1_out_12));  // open: in_1, in_2, in_3, out_10
  _3_input_OR u_3_input_or_2 (
    .in_4(not_1_out_11), .in_5(not_1_out_10), .in_6(not_1_out_12), .in_7(not_1_out_10), .in_8(C),
    .in_9(not_1_out_12), .out_11(n3_input_or_2_out_11), .out_12(n3_input_or_2_out_12));  // open: in_1, in_2, in_3, out_10

  // Notes on the sheet:
  //   B
  //   B
  //   A'
  //   C
  //   A'
  //   C
  //   C'
  //   B
  //   A'
  //   C'
  //   B
  //   A
endmodule

module _3_input_AND (
  input  in_1,
  input  in_2,
  input  in_3,
  input  in_4,
  input  in_5,
  input  in_6,
  input  in_7,
  input  in_8,
  input  in_9,
  output out_10,
  output out_11,
  output out_12
);

  and and_1 (out_10, in_1, in_2, in_3);
  and and_2 (out_11, in_4, in_5, in_6);
  and and_3 (out_12, in_7, in_8, in_9);
endmodule

module _3_input_OR (
  input  in_1,
  input  in_2,
  input  in_3,
  input  in_4,
  input  in_5,
  input  in_6,
  input  in_7,
  input  in_8,
  input  in_9,
  output out_10,
  output out_11,
  output out_12
);

  or or_1 (out_10, in_1, in_2, in_3);
  or or_2 (out_11, in_4, in_5, in_6);
  or or_3 (out_12, in_7, in_8, in_9);
endmodule

module NOT (
  input  in_1,
  input  in_2,
  input  in_3,
  input  in_4,
  input  in_5,
  input  in_6,
  output out_7,
  output out_8,
  output out_9,
  output out_10,
  output out_11,
  output out_12
);

  not not_1 (out_7, in_1);
  not not_2 (out_8, in_2);
  not not_3 (out_9, in_3);
  not not_4 (out_10, in_4);
  not not_5 (out_11, in_5);
  not not_6 (out_12, in_6);
endmodule
