// Logisim project labtask(nand).circ as structural Verilog: 2 circuits, main circuit main
module main (
  input  in_1,
  input  in_2,
  input  in_3,
  input  in_4,
  input  in_5,
  input  in_6,
  input  in_7,
  input  in_8,
  output out_9,
  output out_10,
  output out_11,
  output out_12
);

  nand nand_1 (out_9, in_1, in_2);
  nand nand_2 (out_10, in_3, in_4);
  nand nand_3 (out_11, in_5, in_6);
  nand nand_4 (out_12, in_7, in_8);
endmodule

module IC7400 (
  input  A,
  input  B,
  input  C,
  output out_4
);

  wire main_1_out_9, main_1_out_11, main_1_out_12;

  main main_1 (
    .in_1(B), .in_2(main_1_out_12), .in_3(main_1_out_9), .in_4(main_1_out_11), .in_5(C), .in_6(A), .in_7(C),
    .in_8(C), .out_9(main_1_out_9), .out_10(out_4), .out_11(main_1_out_11), .out_12(main_1_out_12));

  // Notes on the sheet:
  //   (AC)'
  //   (BC')'
  //   y=AC + BC'
endmodule
